// Digital circuit CPU.dig as structural Verilog
module CPU (
  input  clk,
  output [6:0] out_1,
  output [4:0] out_2,
  output [4:0] out_3,
  output [4:0] out_4,
  output [31:0] out_5,
  output [1:0] out_6,
  output out_7,
  output out_8,
  output out_9,
  output [1:0] out_10,
  output out_11,
  output out_12,
  output out_13,
  output out_14,
  output [1:0] out_15,
  output [31:0] out_16,
  output [31:0] out_17,
  output [31:0] out_18,
  output [4:0] out_19,
  output [31:0] out_20,
  output [23:0] out_21,
  output [31:0] pc_o,
  output [31:0] Instruction_Out,
  output [31:0] out_25,
  output [31:0] pc,
  output out_27,
  output [1:0] out_28,
  output [1:0] out_29,
  output [1:0] out_30,
  output [1:0] out_31,
  output [4:0] out_32,
  output [4:0] out_33,
  output [4:0] out_34,
  output [4:0] out_35,
  output [4:0] out_36,
  output out_37,
  output [4:0] out_38,
  output out_39,
  output [1:0] out_40
);

  wire alu_pc, IDEXbubble, IFIDbubble, IFIDfreeze, immSrc, immSrc_out, pc_sel_cu, PCfreeze, RegWrite_IDEX,
       reset, u_comparator_32bit_areequal, u_EX_MEM_Pipeline_memread_out, u_EX_MEM_Pipeline_memwrite_out,
       u_ID_EX_Pipeline_alu_pc_out, u_ID_EX_Pipeline_alusrc_out, u_ID_EX_Pipeline_funct_7_5,
       u_ID_EX_Pipeline_memread_out, u_ID_EX_Pipeline_memwrite_out;
  wire [1:0] MemToReg_EXMEM, MemToReg_IDEX, u_ID_EX_Pipeline_aluop_out, vecSize;
  wire [2:0] u_ID_EX_Pipeline_funct_3_out, u_instruction_parser_funct_3;
  wire [4:0] rd_IDEX, u_ALUControl_aluctrl;
  wire [5:0] multiplexer_4_out;
  wire [6:0] u_instruction_parser_funct_7;
  wire [23:0] novoblocoif2_1_inst_addr;
  wire [31:0] adder_1_s, alu_com_somador_vetorial_1_result_out, barrelshifter_1_out, branch_target,
       eepromdualport_1_d, fw_mux_2_out, imm_out, multiplexer_1_out, multiplexer_2_out, multiplexer_3_out,
       multiplexer_5_out, multiplexer_7_out, multiplexer_8_out, multiplexer_9_out, novoblocoif2_1_pc_out,
       novoblocoif2_1_pc_plus_4, pc_out_in, PC_plus_4, rs1_data_id, rs1_ex_data, rs2_data_id, rs2_ex_data,
       u_EX_MEM_Pipeline_pc_out, u_EX_MEM_Pipeline_writedata_out, u_ID_EX_Pipeline_pc_out,
       u_MEM_WB_Pipeline_pc_out;

  Button button_1 (.out(reset));
  novoblocoIF2 novoblocoif2_1 (
    .jump(out_27), .jump_pc(branch_target), .pc_in(pc), .inst_addr(novoblocoif2_1_inst_addr),
    .pc_out(novoblocoif2_1_pc_out), .PC_plus_4(novoblocoif2_1_pc_plus_4));
  pc #(.applicationType("GHDL")) u_pc (
    .pc_i(novoblocoif2_1_pc_out), .clk(clk), .reset(reset), .freeze(PCfreeze), .pc_o(pc));
  ROM #(.AddrBits(24), .Bits(32)) inst_memory (.A(novoblocoif2_1_inst_addr), .sel(1'b1), .D(out_25));
  IFID #(.applicationType("GHDL")) u_IFID (
    .pc_i(pc), .inst_i(out_25), .clk(clk), .reset(reset), .freeze(IFIDfreeze), .bubble(IFIDbubble),
    .pc4_in(novoblocoif2_1_pc_plus_4), .pc_o(pc_o), .inst_o(Instruction_Out), .pc4_out(PC_plus_4));
  Multiplexer #(.Selector_Bits(2), .Bits(32)) multiplexer_1 (
    .sel(out_30), .in_0(rs1_data_id), .in_1(out_20), .in_2(out_18), .in_3({32{1'b0}}), .out(multiplexer_1_out));
  Multiplexer #(.Selector_Bits(2), .Bits(32)) multiplexer_2 (
    .sel(out_31), .in_0(rs2_data_id), .in_1(out_20), .in_2(out_18), .in_3({32{1'b0}}), .out(multiplexer_2_out));
  Multiplexer #(.Bits(32)) multiplexer_3 (.sel(out_7), .in_0(pc_o), .in_1(multiplexer_1_out), .out(multiplexer_3_out));
  HDU #(.applicationType("GHDL")) u_HDU (
    .rs1(out_2), .rs2(out_3), .opcode(out_1), .jump(out_27), .rd_IDEX(rd_IDEX), .memRead_IDEX(MemToReg_IDEX),
    .regWrite_IDEX(RegWrite_IDEX), .rd_EXMEM(out_36), .memRead_EXMEM(MemToReg_EXMEM), .PC_freeze(PCfreeze),
    .IFID_freeze(IFIDfreeze), .IFID_bubble(IFIDbubble), .IDEX_bubble(IDEXbubble));
  instruction_parser #(.applicationType("GHDL")) u_instruction_parser (
    .instruction_i(Instruction_Out), .opcode_o(out_1), .rd_o(out_4), .funct_3(u_instruction_parser_funct_3),
    .rs1_o(out_2), .rs2_o(out_3), .funct_7(u_instruction_parser_funct_7));
  BarrelShifter #(.Bits(32)) barrelshifter_1 (.in(out_5), .shift(multiplexer_4_out), .out(barrelshifter_1_out));
  Multiplexer #(.Bits(6)) multiplexer_4 (.sel(out_7), .in_0(6'b000001), .in_1({6{1'b0}}), .out(multiplexer_4_out));
  comparator_32bit #(.applicationType("GHDL")) u_comparator_32bit (
    .DataA(multiplexer_1_out), .DataB(multiplexer_2_out), .AreEqual(u_comparator_32bit_areequal));
  branch_condition_unit #(.applicationType("GHDL")) u_branch_condition_unit (
    .funct3(u_instruction_parser_funct_3), .AreEqual(u_comparator_32bit_areequal), .Jump_enable(out_13),
    .Branch_enable(out_12), .pc_write_enable(out_27));
  adder adder_1 (.A(multiplexer_3_out), .B(barrelshifter_1_out), .S(adder_1_s));
  last_bit_zero_aligner #(.applicationType("GHDL")) u_last_bit_zero_aligner (
    .addr_in(adder_1_s), .addr_out(branch_target));
  control_unit #(.applicationType("GHDL")) u_control_unit (
    .opcode(out_1), .alu_op(out_6), .alu_src(out_7), .mem_read(out_8), .mem_write(out_9),
    .mem_to_reg(out_10), .reg_write(out_11), .branch(out_12), .jump(out_13), .pc_sel(pc_sel_cu),
    .alu_pc(alu_pc), .immSrc(immSrc), .vector_size(vecSize));
  register_file #(.applicationType("GHDL")) u_register_file (
    .clk(clk), .reset(reset), .reg_write(out_14), .rs1_addr(out_2), .rs2_addr(out_3), .rd_addr(out_19),
    .rd_data(out_18), .rs1_data(rs1_data_id), .rs2_data(rs2_data_id));
  immediate_extractor #(.applicationType("GHDL")) u_immediate_extractor (
    .instruction_i(Instruction_Out), .immediate_o(out_5));
  ID_EX_Pipeline #(.applicationType("GHDL")) u_ID_EX_Pipeline (
    .clk(clk), .reset(reset), .ALUOp_in(out_6), .ALUSrc_in(out_7), .memRead_in(out_8), .memWrite_in(out_9),
    .memToReg_in(out_10), .regWrite_in(out_11), .Rs1_data_in(rs1_data_id), .Rs2_data_in(rs2_data_id),
    .Imm_in(out_5), .Rs1_in(out_2), .Rs2_in(out_3), .Rd_in(out_4), .funct_3_in(u_instruction_parser_funct_3),
    .funct_7_in(u_instruction_parser_funct_7), .bubble(IDEXbubble), .pc_in(pc_o), .alu_pc_in(alu_pc),
    .pc4_in(PC_plus_4), .immSrc_in(immSrc), .size_in(vecSize), .ALUOp_out(u_ID_EX_Pipeline_aluop_out),
    .ALUSrc_out(u_ID_EX_Pipeline_alusrc_out), .memRead_out(u_ID_EX_Pipeline_memread_out),
    .memWrite_out(u_ID_EX_Pipeline_memwrite_out), .memToReg_out(MemToReg_IDEX), .regWrite_out(RegWrite_IDEX),
    .Rs1_data_out(rs1_ex_data), .Rs2_data_out(rs2_ex_data), .Imm_out(imm_out), .Rs1_out(out_32),
    .Rs2_out(out_33), .Rd_out(rd_IDEX), .funct_3_out(u_ID_EX_Pipeline_funct_3_out),
    .funct_7_5(u_ID_EX_Pipeline_funct_7_5), .pc_out(u_ID_EX_Pipeline_pc_out),
    .alu_pc_out(u_ID_EX_Pipeline_alu_pc_out), .pc4_out(pc_out_in), .immSrc_out(immSrc_out), .size_out(out_40));
  Multiplexer #(.Bits(32)) multiplexer_5 (
    .sel(u_ID_EX_Pipeline_alusrc_out), .in_0(fw_mux_2_out), .in_1(imm_out), .out(multiplexer_5_out));
  Multiplexer #(.Selector_Bits(2), .Bits(32)) multiplexer_6 (
    .sel(out_29), .in_0(rs2_ex_data), .in_1(out_20), .in_2(out_18), .in_3({32{1'b0}}), .out(fw_mux_2_out));
  ALUControl #(.applicationType("GHDL")) u_ALUControl (
    .ALUOp(u_ID_EX_Pipeline_aluop_out), .funct3(u_ID_EX_Pipeline_funct_3_out),
    .funct7_5(u_ID_EX_Pipeline_funct_7_5), .size(out_40), .ALUCtrl(u_ALUControl_aluctrl));
  Multiplexer #(.Bits(32)) multiplexer_7 (
    .sel(u_ID_EX_Pipeline_alu_pc_out), .in_0(multiplexer_8_out), .in_1(u_ID_EX_Pipeline_pc_out),
    .out(multiplexer_7_out));
  Multiplexer #(.Selector_Bits(2), .Bits(32)) multiplexer_8 (
    .sel(out_28), .in_0(rs1_ex_data), .in_1(out_20), .in_2(out_18), .in_3({32{1'b0}}), .out(multiplexer_8_out));
  forwarding_unit #(.applicationType("GHDL")) u_forwarding_unit (
    .ID_EX_rs1(out_32), .ID_EX_rs2(out_33), .IF_ID_rs1(out_2), .IF_ID_rs2(out_3), .EX_MEM_rd(out_36),
    .EX_MEM_RegWrite(out_37), .MEM_WB_rd(out_19), .MEM_WB_RegWrite(out_14), .ForwardA(out_28),
    .ForwardB(out_29), .Forward_ID_A(out_30), .Forward_ID_B(out_31));
  Alu_com_somador_vetorial alu_com_somador_vetorial_1 (
    .a(multiplexer_7_out), .b(multiplexer_5_out), .c(u_ALUControl_aluctrl),
    .result_out(alu_com_somador_vetorial_1_result_out));
  Multiplexer #(.Bits(32)) multiplexer_9 (
    .sel(immSrc_out), .in_0(alu_com_somador_vetorial_1_result_out), .in_1(imm_out), .out(multiplexer_9_out));
  EX_MEM_Pipeline #(.applicationType("GHDL")) u_EX_MEM_Pipeline (
    .clk(clk), .reset(reset), .MemRead_in(u_ID_EX_Pipeline_memread_out),
    .MemWrite_in(u_ID_EX_Pipeline_memwrite_out), .MemToReg_in(MemToReg_IDEX), .RegWrite_in(RegWrite_IDEX),
    .ALUResult_in(multiplexer_9_out), .WriteData_in(fw_mux_2_out), .Rd_in(rd_IDEX), .bubble(1'b0),
    .pc_in(pc_out_in), .MemRead_out(u_EX_MEM_Pipeline_memread_out),
    .MemWrite_out(u_EX_MEM_Pipeline_memwrite_out), .MemToReg_out(MemToReg_EXMEM), .RegWrite_out(out_37),
    .ALUResult_out(out_20), .WriteData_out(u_EX_MEM_Pipeline_writedata_out), .Rd_out(out_36),
    .pc_out(u_EX_MEM_Pipeline_pc_out));
  addr_trunc32to24 #(.applicationType("GHDL")) u_addr_trunc32to24 (.addr_32(out_20), .addr_24(out_21));
  EEPROMDualPort #(.AddrBits(24), .Bits(32)) eepromdualport_1 (
    .A(out_21), .Din(u_EX_MEM_Pipeline_writedata_out), .str(u_EX_MEM_Pipeline_memwrite_out), .C(clk),
    .ld(u_EX_MEM_Pipeline_memread_out), .D(eepromdualport_1_d));
  MEM_WB_Pipeline #(.applicationType("GHDL")) u_MEM_WB_Pipeline (
    .clk(clk), .reset(reset), .MemToReg_in(MemToReg_EXMEM), .RegWrite_in(out_37),
    .ReadData_in(eepromdualport_1_d), .ALUResult_in(out_20), .Rd_in(out_36),
    .pc_in(u_EX_MEM_Pipeline_pc_out), .MemToReg_out(out_15), .RegWrite_out(out_14), .ALUResult_out(out_16),
    .ReadData_out(out_17), .Rd_out(out_19), .pc_out(u_MEM_WB_Pipeline_pc_out));
  Multiplexer #(.Selector_Bits(2), .Bits(32)) multiplexer_10 (
    .sel(out_15), .in_0(out_16), .in_1(out_17), .in_2(u_MEM_WB_Pipeline_pc_out), .in_3({32{1'b0}}),
    .out(out_18));

  assign out_34 = out_2;
  assign out_35 = out_3;
  assign out_38 = out_19;
  assign out_39 = out_14;

  // Other names for the same wires on the sheet: ALUResult_EXMEM[31:0] = out_20; branch = out_12;
  //   fw_alu_a[1:0] = out_28; fw_alu_b[1:0] = out_29; fw_id_a[1:0] = out_30; fw_id_b[1:0] = out_31;
  //   hdu_opcode[6:0] = out_1; jump = out_13; pc_in[31:0] = pc_o; pc_sel_res = out_27; rd_data_wb[31:0] = out_18;
  //   rd_EXMEM[4:0] = out_36; rd_MEMWB[4:0] = out_19; RegWrite_EXMEM = out_37; RegWrite_MEMWB = out_14;
  //   rs1_ex[4:0] = out_32; rs1_id[4:0] = out_2; rs2_ex[4:0] = out_33; rs2_id[4:0] = out_3

  // Notes on the sheet:
  //   pc_o: Saída PC do registrador IF/ID
  //   Instruction_Out: Saída instruction do registrador IF/ID
  //   pc: Valor atual de PC
  //   Estágio IF
  //   contents of inst_memory (hex, n*v repeats v):
  //   1001d4,302123,14*0,2903,190913,100993,98513,30000e7,9a503,2a583
  //   ,a2a023,b9a023,198993,ff2999e3,6f,52583,50293,50613,62683,40b68733
  //   ,1f75713,70363,68593,60293,160613,ff2619e3,8067
  //   contents of eepromdualport_1 (hex, n*v repeats v):
  //   8*a
endmodule

/* Code of pc:
-- Registrador de 32 bits com entradas PCin, clk, reset e saída PCout

library IEEE;
use IEEE.STD_LOGIC_1164.ALL;

entity pc is
	Port (
    	pc_i : in std_logic_vector(31 downto 0);
    	clk: in std_logic;
        reset: in std_logic;

		freeze: in std_logic;

        pc_o: out std_logic_vector(31 downto 0)
    	);
end pc;

architecture Behavioral of pc is

begin

process(clk, reset)
begin
	if reset = '1' then
		pc_o <= X"00000000";

	elsif rising_edge(clk) and freeze = '0' then

		pc_o <= pc_i;

	end if;
end process;

end Behavioral;
*/

/* Code of IFID:
-- Registrador que guarda os dados necessários entre IF e ID. Esses dados são o valor de PC e a instrução da vez
library IEEE;
use IEEE.STD_LOGIC_1164.ALL;

entity IFID is
	Port (
    	pc_i : in std_logic_vector(31 downto 0);
        inst_i: in std_logic_vector(31 downto 0);

    	clk: in std_logic;
        reset: in std_logic;

		freeze: in std_logic;
		bubble: in std_logic;
	pc4_in: in std_logic_vector(31 downto 0);

        pc_o: out std_logic_vector(31 downto 0);
        inst_o: out std_logic_vector(31 downto 0);
	pc4_out: out std_logic_vector(31 downto 0)
	
    	);
end IFID;

architecture Behavioral of IFID is

begin

process(clk, reset)
begin
	if reset = '1' then
        pc_o <= X"00000000";
        inst_o <= X"00000000";
	pc4_out <= X"00000000";

	elsif rising_edge(clk) then

		if freeze = '0' then
			if bubble = '1' then
				pc_o <= X"00000000";
				inst_o <= X"00000000";
				pc4_out <= X"00000000";
			else
				pc_o <= pc_i;
				inst_o <= inst_i;
				pc4_out <= pc4_in;
			end if;
		end if;

	end if;
end process;

end Behavioral;
*/

/* Code of HDU:
library IEEE;
use IEEE.STD_LOGIC_1164.ALL;

entity HDU is
	Port (
        -- Entradas que vêm do estágio ID
        rs1: in std_logic_vector(4 downto 0);
        rs2: in std_logic_vector(4 downto 0);
        opcode: in std_logic_vector(6 downto 0);

        jump: in std_logic; -- Indica se será feito um salto este ciclo

        -- Entradas que vêm dos demais estágios
        rd_IDEX: in std_logic_vector(4 downto 0);
        memRead_IDEX: in std_logic_vector(1 downto 0);
        regWrite_IDEX: in std_logic;

        rd_EXMEM: in std_logic_vector(4 downto 0);
        memRead_EXMEM: in std_logic_vector(1 downto 0);

    	-- Saídas
        -- Saídas freeze
        -- Se uma delas é '1', o registrador em questão mantém seu valor atual no próximo ciclo
        PC_freeze: out std_logic;
        IFID_freeze: out std_logic;

        -- Saídas bubble
        -- Se uma delas é '1', o registrador em questão recebe um NOP no próximo ciclo. Seu valor atual pode continuar se propagando ao longo da pipeline (pois o NOP é inserido de forma síncrona)
        IFID_bubble: out std_logic;
        IDEX_bubble: out std_logic
    	);
end HDU;

architecture Behavioral of HDU is

    -- Opcodes para diferentes tipos de instrução
    constant R_TYPE_OP   : std_logic_vector(6 downto 0) := "0110011"; -- OP (ADD, SUB, AND, OR, XOR)
    constant I_TYPE_OP   : std_logic_vector(6 downto 0) := "0010011"; -- OP-IMM (ADDI, ANDI, ORI)
    constant L_TYPE_OP   : std_logic_vector(6 downto 0) := "0000011"; -- LOAD (LW)
    constant S_TYPE_OP   : std_logic_vector(6 downto 0) := "0100011"; -- STORE (SW)
    constant B_TYPE_OP   : std_logic_vector(6 downto 0) := "1100011"; -- BRANCH (BEQ, BNE)
    constant JAL_OP      : std_logic_vector(6 downto 0) := "1101111"; -- JAL
    constant JALR_OP     : std_logic_vector(6 downto 0) := "1100111"; -- JALR
    constant LUI_OP      : std_logic_vector(6 downto 0) := "0110111"; -- LUI
    constant AUIPC_OP    : std_logic_vector(6 downto 0) := "0010111"; -- AUIPC

    constant VECTOR_R_OP4B   : std_logic_vector(6 downto 0) := "1010000";
    constant VECTOR_R_OP8B   : std_logic_vector(6 downto 0) := "1010001";
    constant VECTOR_R_OP16B  : std_logic_vector(6 downto 0) := "1010010";
    constant VECTOR_I_OP4B   : std_logic_vector(6 downto 0) := "1010100";
    constant VECTOR_I_OP8B   : std_logic_vector(6 downto 0) := "1010101";
    constant VECTOR_I_OP16B  : std_logic_vector(6 downto 0) := "1010110";
    constant VECTOR_U_OP4B   : std_logic_vector(6 downto 0) := "1011000";
    constant VECTOR_U_OP8B   : std_logic_vector(6 downto 0) := "1011001";
    constant VECTOR_U_OP16B  : std_logic_vector(6 downto 0) := "1011010";

begin

process(rs1, rs2, opcode, jump, rd_IDEX, memRead_IDEX, regWrite_IDEX, rd_EXMEM, memRead_EXMEM)

    variable inst_type: integer;

    -- Temos dois tipos de hazard: DataHazard e ControlHazard
    -- DataHazard ocorre em três situações: load-use, write-jump e load-jump
    -- ControlHazard ocorre em jump

    -- inst_type = 1 indica que a instrução é jal, auipc, lui, ou seja, não está sujeita a DataHazard

    -- inst_type = 2 indica que a instrução é addi, andi, ori, xori, lli, srli, lw, sw, ou seja, está sujeita a DataHazard (load-use) apenas em rs1

    -- inst_type = 3 indica que a instrução é add, sub, and, or, xor, sll, srl, ou seja, está sujeita a DataHazard (load-use) em rs1 e rs2

    -- inst_type = 4 indica que a instrução é jalr, ou seja, está sujeita a DataHazard (load-branch ou write-branch) apenas em rs1

    -- inst_type = 5 indica que a instrução é beq, bne, ou seja, está sujeita a DataHazard (load-branch ou write-branch) em rs1 e rs2

    variable DataHazard: std_logic; -- Indica que há um DataHazard

begin
    -- Identificar se a instução em ID é tipo 1, 2, ou 3
    case opcode is
        when JAL_OP | LUI_OP | AUIPC_OP | VECTOR_U_OP4B | VECTOR_U_OP8B | VECTOR_U_OP16B =>
            inst_type := 1;
        when I_TYPE_OP | L_TYPE_OP | S_TYPE_OP | VECTOR_I_OP4B | VECTOR_I_OP8B | VECTOR_I_OP16B =>
            inst_type := 2;
        when R_TYPE_OP | VECTOR_R_OP4B | VECTOR_R_OP8B | VECTOR_R_OP16B =>
            inst_type := 3;
        when JALR_OP =>
            inst_type := 4;
        when B_TYPE_OP =>
            inst_type := 5;
        when others =>
            -- No caso de instrução inválida, vou considerar como tipo 1 (não suscetível a hazard de escrita-leitura)
            inst_type := 1;
    end case;

    -- Identificar com base nisso se há DataHazard
    case inst_type is            
        when 2 =>
            if memRead_IDEX = "01" and rd_IDEX = rs1 then
                DataHazard := '1'; -- load-use
            else
                DataHazard := '0';
            end if;

        when 3 =>
            if memRead_IDEX = "01" and (rd_IDEX = rs1 or rd_IDEX = rs2) then
                DataHazard := '1'; -- load-use
            else
                DataHazard := '0';
            end if;

        when 4 =>
            if regWrite_IDEX = '1' and rd_IDEX = rs1 then
                DataHazard := '1'; -- write-jump

            elsif memRead_IDEX = "01" and rd_IDEX = rs1 then
                DataHazard := '1'; -- load-jump em IDEX
            
            elsif memRead_EXMEM = "01" and rd_EXMEM = rs1 then
                DataHazard := '1'; -- load-jump em EXMEM
            
            else
                DataHazard := '0';

            end if;

        when 5 =>
            if regWrite_IDEX = '1' and (rd_IDEX = rs1 or rd_IDEX = rs2) then
                DataHazard := '1'; -- write-jump

            elsif memRead_IDEX = "01" and (rd_IDEX = rs1 or rd_IDEX = rs2) then
                DataHazard := '1'; -- load-jump em IDEX

            elsif memRead_EXMEM = "01" and (rd_EXMEM = rs1 or rd_EXMEM = rs2) then
                DataHazard := '1'; -- load-jump em EXMEM
            
            else
                DataHazard := '0';

            end if;

        when others =>
            -- No tipo 1, não temos DataHazard
            DataHazard := '0';
    end case;

    -- De acordo com DataHazard e jump, determinar as saídas
    if DataHazard = '1' then
        PC_freeze <= '1';
        IFID_freeze <= '1';
        IFID_bubble <= '0';
        IDEX_bubble <= '1';
    elsif jump = '1' then
        PC_freeze <= '0';
        IFID_freeze <= '0';
        IFID_bubble <= '1';
        IDEX_bubble <= '0';
    else
        PC_freeze <= '0';
        IFID_freeze <= '0';
        IFID_bubble <= '0';
        IDEX_bubble <= '0';
    end if;
end process;

end Behavioral;
*/

/* Code of instruction_parser:
library ieee;
use ieee.std_logic_1164.all;

entity instruction_parser is
    port (
        instruction_i : in  std_logic_vector(31 downto 0); -- 32-bit RISC-V instruction

        -- Extracted fields
        opcode_o      : out std_logic_vector(6 downto 0);  -- bits 6-0
        rd_o          : out std_logic_vector(4 downto 0);  -- bits 11-7
        funct_3       : out std_logic_vector(2 downto 0);  -- bits 14-12
        rs1_o         : out std_logic_vector(4 downto 0);  -- bits 19-15
        rs2_o         : out std_logic_vector(4 downto 0); -- bits 24-20
        funct_7       : out std_logic_vector(6 downto 0)
    );
end entity instruction_parser;

architecture behavioral of instruction_parser is
begin

    -- Simple direct assignments for common fields
    opcode_o <= instruction_i(6 downto 0);
    rd_o     <= instruction_i(11 downto 7);
    funct_3  <= instruction_i(14 downto 12);
    rs1_o    <= instruction_i(19 downto 15);
    rs2_o    <= instruction_i(24 downto 20);
    funct_7  <= instruction_i(31 downto 25);

end architecture behavioral;
*/

/* Code of comparator_32bit:
library ieee;
use ieee.std_logic_1164.all;

-- The entity declaration for the comparator
entity comparator_32bit is
    port (
        -- Inputs: The two 32-bit data values to compare.
        -- These will come from the register file (reading rs1 and rs2).
        DataA   : in  std_logic_vector(31 downto 0);
        DataB   : in  std_logic_vector(31 downto 0);

        -- Output: A single bit indicating the result of the comparison.
        -- '1' if DataA is equal to DataB.
        -- '0' if DataA is not equal to DataB.
        AreEqual : out std_logic
    );
end entity comparator_32bit;

-- Architecture definition for the comparator
architecture behavioral of comparator_32bit is
begin

    -- This is a purely combinational process.
    -- It continuously compares the two input vectors.
    process(DataA, DataB)
    begin
        -- The comparison logic is straightforward.
        -- If the two input vectors are identical, the output is '1'.
        -- Otherwise, the output is '0'.
        -- This can be implemented efficiently by synthesizers.
        if DataA = DataB then
            AreEqual <= '1';
        else
            AreEqual <= '0';
        end if;
    end process;

    -- Alternative (and more concise) concurrent assignment statement:
    -- AreEqual <= '1' when DataA = DataB else '0';

end architecture behavioral;
*/

/* Code of branch_condition_unit:
library ieee;
use ieee.std_logic_1164.all;

entity branch_condition_unit is -- Renamed for broader scope (branch and jump)
    port (
        -- Inputs
        funct3      : in  std_logic_vector(2 downto 0); -- funct3 field from the instruction
        AreEqual    : in  std_logic;                    -- Result from an ALU/comparator: '1' if rs1 = rs2 (i.e., rs1 - rs2 = 0), '0' otherwise
        Jump_enable : in  std_logic;                    -- Control signal: '1' if the current instruction is a jump (e.g., JAL, JALR)
        Branch_enable : in  std_logic;                  -- Control signal: '1' if the current instruction is a branch (e.g., BEQ, BNE, BLT, BGE, etc.)

        -- Output for controlling PC update via MUX
        pc_write_enable : out std_logic                 -- '1' if the PC should be updated with a new target address
                                                        -- (either due to a taken branch or any jump instruction), '0' otherwise
    );
end entity branch_condition_unit;

architecture behavioral of branch_condition_unit is
begin

    -- Logic for determining if the PC should be updated with a new target address
    process(funct3, AreEqual, Jump_enable, Branch_enable)
    begin
        -- Default to not taking a branch/jump
        pc_write_enable <= '0';

        -- If it's a jump instruction, always enable PC write (JAL, JALR)
        if Jump_enable = '1' then
            pc_write_enable <= '1';
        elsif Branch_enable = '1' then -- Only evaluate branch conditions if it's a branch instruction
            case funct3 is
                -- BEQ: Branch if Equal (funct3 = 000)
                when "000" =>
                    if AreEqual = '1' then
                        pc_write_enable <= '1';
                    else
                        pc_write_enable <= '0';
                    end if;

                -- BNE: Branch if Not Equal (funct3 = 001)
                when "001" =>
                    if AreEqual = '0' then
                        pc_write_enable <= '1';
                    else
                        pc_write_enable <= '0';
                    end if;

                -- You can add other branch types here if needed (e.g., BLT, BGE, BLTU, BGEU)
                -- These would require additional inputs for ALU flags (e.g., LessThan, GreaterThan)
                -- For example:
                -- when "100" => -- BLT
                --    if LessThan = '1' then
                --        pc_write_enable <= '1';
                --    end if;

                when others =>
                    -- For any other funct3 value when Branch_enable is '1' (e.g., unsupported branch type)
                    pc_write_enable <= '0';
            end case;
        else
            -- If neither Jump_enable nor Branch_enable is '1',
            -- then it's a sequential instruction, and pc_write_enable remains '0' (default)
            pc_write_enable <= '0';
        end if;
    end process;

end architecture behavioral;
*/

/* Code of last_bit_zero_aligner:
library IEEE;
use IEEE.STD_LOGIC_1164.ALL;

entity last_bit_zero_aligner is
    -- O Digital estava dando problema, como se WIDTH_G fosse 1 a despeito de seu valor default. Tirei o generic
    port (
        -- Input: The address that needs alignment
        addr_in  : in  STD_LOGIC_VECTOR(31 downto 0);
        -- Output: The aligned address with the LSB cleared
        addr_out : out STD_LOGIC_VECTOR(31 downto 0)
    );
end entity last_bit_zero_aligner;

architecture behavioral of last_bit_zero_aligner is
begin

    addr_out <= addr_in(31 downto 1) & '0';

end architecture behavioral;
*/

/* Code of control_unit:
library ieee;
use ieee.std_logic_1164.all;

entity control_unit is
    port (
        -- Inputs
        opcode      : in  std_logic_vector(6 downto 0); -- 7-bit opcode from the instruction

        -- Outputs: Control signals for the datapath
        alu_op      : out std_logic_vector(1 downto 0); -- Controls the ALU's main operation:
                                                        -- "00" = Add (for Loads/Stores/AUIPC/LUI/JAL/JALR address calc or pass-through)
                                                        -- "01" = Subtract (for Branches for comparison)
                                                        -- "10" = R-type operation (further decoded by funct3/funct7)
                                                        -- "11" = I-type operation (further decoded by funct3)
        alu_src     : out std_logic;                    -- Selects the second ALU source:
                                                        -- '0' = rs2 data (for R-type)
                                                        -- '1' = immediate (for I, S, B, U, J-types)
        mem_read    : out std_logic;                    -- Enables reading from data memory
        mem_write   : out std_logic;                    -- Enables writing to data memory
        mem_to_reg  : out std_logic_vector(1 downto 0);                    -- Selects if data from memory goes to the register file (for loads)
        reg_write   : out std_logic;                    -- Enable writing to the register file
        branch      : out std_logic;                    -- Indicates a conditional branch instruction (for enabling branch logic)
        jump        : out std_logic;                    -- Indicates an unconditional jump instruction (JAL, JALR)
        pc_sel      : out std_logic;                     -- Selects next PC: '0' = PC+4, '1' = Branch/Jump Target
        alu_pc       : out std_logic;
        immSrc      : out std_logic;
        vector_size  : out std_logic_vector(1 downto 0) -- Selects the vector size for vector operations:
                                                        -- "00" = 4 bytes, "01" = 8 bytes, "10" = 16 bytes, "11" = 32 bytes
    );
end entity control_unit;

architecture behavioral of control_unit is
    -- Define the opcodes for different instruction types as constants for readability
    constant R_TYPE_OP   : std_logic_vector(6 downto 0) := "0110011"; -- OP (e.g., ADD, SUB, AND, OR, XOR)
    constant I_TYPE_OP   : std_logic_vector(6 downto 0) := "0010011"; -- OP-IMM (e.g., ADDI, ANDI, ORI)
    constant L_TYPE_OP   : std_logic_vector(6 downto 0) := "0000011"; -- LOAD (e.g., LW)
    constant S_TYPE_OP   : std_logic_vector(6 downto 0) := "0100011"; -- STORE (e.g., SW)
    constant B_TYPE_OP   : std_logic_vector(6 downto 0) := "1100011"; -- BRANCH (e.g., BEQ, BNE)
    constant JAL_OP      : std_logic_vector(6 downto 0) := "1101111"; -- JAL (Jump and Link)
    constant JALR_OP     : std_logic_vector(6 downto 0) := "1100111"; -- JALR (Jump and Link Register)
    constant LUI_OP      : std_logic_vector(6 downto 0) := "0110111"; -- LUI (Load Upper Immediate)
    constant AUIPC_OP    : std_logic_vector(6 downto 0) := "0010111"; -- AUIPC (Add Upper Immediate to PC)
    constant VECTOR_R_OP4B   : std_logic_vector(6 downto 0) := "1010000"; -- Vectorial operations (custom opcode) - 4 bits
    constant VECTOR_R_OP8B   : std_logic_vector(6 downto 0) := "1010001"; -- Vectorial operations (custom opcode) - 8 bits
    constant VECTOR_R_OP16B  : std_logic_vector(6 downto 0) := "1010010"; -- Vectorial operations (custom opcode) - 16 bits
    constant VECTOR_I_OP4B   : std_logic_vector(6 downto 0) := "1010100"; -- Vectorial operations with immediate (custom opcode) - 4 bits
    constant VECTOR_I_OP8B   : std_logic_vector(6 downto 0) := "1010101"; -- Vectorial operations with immediate (custom opcode) - 8 bits
    constant VECTOR_I_OP16B  : std_logic_vector(6 downto 0) := "1010110"; -- Vectorial operations with immediate (custom opcode) - 16 bits
    constant VECTOR_U_OP4B  : std_logic_vector(6 downto 0) := "1011000"; -- Vectorial operations with immediate (custom opcode) - 4 bits
    constant VECTOR_U_OP8B  : std_logic_vector(6 downto 0) := "1011001"; -- Vectorial operations with immediate (custom opcode) - 8 bits
    constant VECTOR_U_OP16B : std_logic_vector(6 downto 0) := "1011010"; -- Vectorial operations with immediate (custom opcode) - 16 bits

begin

    -- Main control logic process.
    -- This process is sensitive to 'opcode'.
    -- All output signals must be assigned within this single process to avoid latches.
    process(opcode)
    begin
        -- safe default (e.g., NOP-like behavior, no writes, no branches/jumps).
        reg_write  <= '0';
        mem_to_reg <= "00";
        mem_read   <= '0';
        mem_write  <= '0';
        alu_src    <= '0';
        branch     <= '0';
        jump       <= '0';
        pc_sel     <= '0'; -- Default to PC+4
        alu_op     <= "00"; -- Default to "00" (Add/Pass-through) for ALU
        alu_pc     <= '0';
        immSrc	   <= '0';
        vector_size <= "11"; -- Default vector size (32 bytes)

        -- Use a case statement to decode the opcode and assert specific control signals.
        case opcode is
            -- R-Type instructions (e.g., ADD, SUB, AND, OR)
            when R_TYPE_OP =>
                reg_write  <= '1';
                alu_src    <= '0';
                alu_op     <= "10";

            -- I-Type instructions (Arithmetic/Logical with Immediate, excluding Loads/JALR)
            when I_TYPE_OP =>
                reg_write  <= '1';
                alu_src    <= '1';
                alu_op     <= "11";

            -- Load instructions (I-type, e.g., LW)
            when L_TYPE_OP =>
                reg_write  <= '1';
                mem_to_reg <= "01";
                mem_read   <= '1';
                alu_src    <= '1';
                alu_op     <= "00";

            -- Store instructions (S-type, e.g., SW)
            when S_TYPE_OP =>
                mem_write  <= '1';
                alu_src    <= '1';
                alu_op     <= "00";

            -- Branch instructions (B-type, e.g., BEQ, BNE)
            when B_TYPE_OP =>
                branch     <= '1';    -- This signal enables the branch comparison logic
                pc_sel     <= '1';    -- Take jump target (maybe)
                alu_op     <= "01";   -- ALU performs subtraction (for comparison)

            -- LUI (Load Upper Immediate)
            when LUI_OP =>
                reg_write  <= '1';
		        immSrc	   <= '1';

            -- AUIPC (Add Upper Immediate to PC)
            when AUIPC_OP =>
                reg_write  <= '1';
                alu_src    <= '1';
                alu_op     <= "00";
		        alu_pc     <= '1';

            -- JAL (Jump and Link)
            when JAL_OP =>
                reg_write  <= '1';
                jump       <= '1';    -- This signal indicates an unconditional jump
                pc_sel     <= '1';    -- Take jump target 
                alu_op     <= "00";   -- ALU may be used to calculate target address (PC + immediate) or pass PC+4
		        mem_to_reg <= "10";

            -- JALR (Jump and Link Register)
            when JALR_OP =>
                reg_write  <= '1';
                jump       <= '1';    -- This signal indicates an unconditional jump
                pc_sel     <= '1';    -- Take jump target 
                alu_src    <= '1';    -- Immediate is used by ALU (for address calculation)
                alu_op     <= "00";   -- ALU performs addition (rs1 + immediate)
		        mem_to_reg <= "10";

            -- Vector R operations (custom opcodes)
            when VECTOR_R_OP4B | 
                 VECTOR_R_OP8B | 
                 VECTOR_R_OP16B =>
                
                reg_write  <= '1';
                alu_src    <= '0';
                alu_op     <= "10";

                case opcode is
                    when VECTOR_R_OP4B =>
                        vector_size <= "00"; -- 4 bytes
                    when VECTOR_R_OP8B =>
                        vector_size <= "01"; -- 8 bytes
                    when VECTOR_R_OP16B =>
                        vector_size <= "10"; -- 16 bytes
                    when others =>
                        vector_size <= "11"; -- Default to 32 bytes
                end case;

            -- Vector I operations (custom opcodes)
            when VECTOR_I_OP4B | 
                 VECTOR_I_OP8B | 
                 VECTOR_I_OP16B =>

                reg_write  <= '1';
                alu_src    <= '1';
                alu_op     <= "11";

                case opcode is
                    when VECTOR_I_OP4B =>
                        vector_size <= "00"; -- 4 bytes
                    when VECTOR_I_OP8B =>
                        vector_size <= "01"; -- 8 bytes
                    when VECTOR_I_OP16B =>
                        vector_size <= "10"; -- 16 bytes
                    when others =>
                        vector_size <= "11"; -- Default to 32 bytes
                end case;

            -- Vector U operations (custom opcodes)
            when VECTOR_U_OP4B | 
                 VECTOR_U_OP8B | 
                 VECTOR_U_OP16B =>

                reg_write  <= '1';
                alu_src    <= '1';
                alu_op     <= "00";
                alu_pc     <= '1';

                case opcode is
                    when VECTOR_U_OP4B =>
                        vector_size <= "00"; -- 4 bytes
                    when VECTOR_U_OP8B =>
                        vector_size <= "01"; -- 8 bytes
                    when VECTOR_U_OP16B =>
                        vector_size <= "10"; -- 16 bytes
                    when others =>
                        vector_size <= "11"; -- Default to 32 bytes
                end case;

            when others =>
                null;
        end case;
    end process;

end architecture behavioral;
*/

/* Code of register_file:
library ieee;
use ieee.std_logic_1164.all;
use ieee.numeric_std.all;

entity register_file is
    port (
        -- System signals
        clk      : in  std_logic;
        reset    : in  std_logic; -- Asynchronous reset

        -- Write Port
        reg_write: in  std_logic; -- Control signal to enable writing
        rd_addr  : in  std_logic_vector(4 downto 0);
        rd_data  : in  std_logic_vector(31 downto 0);

        -- Read Port 1
        rs1_addr : in  std_logic_vector(4 downto 0);
        rs1_data : out std_logic_vector(31 downto 0);

        -- Read Port 2
        rs2_addr : in  std_logic_vector(4 downto 0);
        rs2_data : out std_logic_vector(31 downto 0)
    );
end entity register_file;

architecture behavioral of register_file is

    -- The core storage for the 32 registers.
    type reg_array is array (0 to 31) of std_logic_vector(31 downto 0);
    signal registers : reg_array := (others => (others => '0'));

begin

    write_proc: process(clk, reset)
    begin
        -- Asynchronously reset all registers to zero.
        if reset = '1' then
            -- Using a loop for clarity; (others => (others => '0')) is also valid.
            for i in 0 to 31 loop
                registers(i) <= (others => '0');
            end loop;
        -- On the rising edge of the clock, perform the write operation.
        elsif rising_edge(clk) then
            -- Check if the write enable signal is active and the destination
            -- is not the hardwired-zero register (r0).
            if reg_write = '1' and rd_addr /= "00000" then
                registers(to_integer(unsigned(rd_addr))) <= rd_data;
            end if;
        end if;
    end process write_proc;


    -- This is achieved by "forwarding" the write data directly to the output
    -- if a read is requested for the address that is currently being written to.


    -- Read Port 1 Logic
    rs1_data <=
        -- CASE 1: Forwarding Condition
        -- If we are writing (reg_write='1') to a valid register (rd_addr /= 0)
        -- AND the address we are writing to is the same as the address we are
        -- reading from (rd_addr = rs1_addr), then forward the input data (rd_data).
        rd_data when (reg_write = '1' and rd_addr = rs1_addr and rd_addr /= "00000") else

        -- CASE 2: Normal Read from Register File
        -- If we are reading from register 0, output all zeros.
        -- Otherwise, output the value stored in the specified register.
        (others => '0') when (rs1_addr = "00000") else
        registers(to_integer(unsigned(rs1_addr)));

    -- Read Port 2 Logic (Identical logic to Read Port 1)
    rs2_data <=
        -- CASE 1: Forwarding Condition
        rd_data when (reg_write = '1' and rd_addr = rs2_addr and rd_addr /= "00000") else

        -- CASE 2: Normal Read from Register File
        (others => '0') when (rs2_addr = "00000") else
        registers(to_integer(unsigned(rs2_addr)));

end architecture behavioral;
*/

/* Code of immediate_extractor:
library ieee;
use ieee.std_logic_1164.all;
use ieee.numeric_std.all; -- For signed arithmetic and type conversions

entity immediate_extractor is
    port (
        instruction_i : in  std_logic_vector(31 downto 0); -- 32-bit RISC-V instruction input
        immediate_o   : out std_logic_vector(31 downto 0)  -- 32-bit sign-extended immediate output
    );
end entity immediate_extractor;

architecture behavioral of immediate_extractor is
    -- Internal signal to hold the opcode (bits 6 downto 0) for use in the process.
    signal opcode_s : std_logic_vector(6 downto 0);
begin

    -- Extract the opcode from the instruction. This assignment is concurrent.
    opcode_s <= instruction_i(6 downto 0);

    -- This process block implements the combinational logic for immediate extraction.
    -- The sensitivity list includes all signals that, when changed, should
    -- re-evaluate the logic inside the process.
    process(instruction_i, opcode_s)
        -- Declare a local variable to build the immediate value before assigning it
        -- to the output signal. Variables are evaluated immediately within the process.
        variable imm : std_logic_vector(31 downto 0);
    begin
        -- Use a case statement to select the immediate extraction logic
        -- based on the instruction's opcode.
        case opcode_s is
            -- I-type immediate (Load, Op-Imm, JALR)
            -- Opcode values: 0x03 (LOAD), 0x13 (OP-IMM), 0x67 (JALR)
            -- Format: imm[11:0] is instruction[31:20]
            when "0000011" | "0010011" | "1100111" =>
                -- Sign-extend the 12-bit immediate: replicate bit 31 of the instruction
                -- (which is imm[11]) across the higher bits (31 downto 12) of the 32-bit immediate.
                imm := (others => instruction_i(31));
                -- Place the 12-bit immediate into the lower 12 bits of 'imm'.
                imm(11 downto 0) := instruction_i(31 downto 20);
                -- Assign the constructed immediate to the output.
                immediate_o <= imm;

            -- S-type immediate (Store)
            -- Opcode value: 0x23 (STORE)
            -- Format: imm[11:5] from instruction[31:25], imm[4:0] from instruction[11:7]
            -- Reconstructed: imm[11:5] << 5 | imm[4:0]
            when "0100011" =>
                -- Sign-extend the 12-bit immediate: use bit 31 of the instruction
                -- (which is imm[11]) for sign extension.
                imm := (others => instruction_i(31));
                -- Place the high part of the immediate (imm[11:5]) into its position.
                imm(11 downto 5) := instruction_i(31 downto 25);
                -- Place the low part of the immediate (imm[4:0]) into its position.
                imm(4 downto 0)  := instruction_i(11 downto 7);
                -- Assign the constructed immediate to the output.
                immediate_o <= imm;

            -- B-type immediate (Branch)
            -- Opcode value: 0x63 (BRANCH)
            -- Format: imm[12|10:5|4:1|11]
            -- Bits: instruction[31] (imm[12]), instruction[30:25] (imm[10:5]),
            --       instruction[11:8] (imm[4:1]), instruction[7] (imm[11])
            -- Reconstructed: imm[12] << 12 | imm[11] << 11 | imm[10:5] << 5 | imm[4:1] << 1 (imm[0] is always '0')
            when "1100011" =>
                -- Sign-extend the 13-bit immediate: use bit 31 of the instruction
                -- (which is imm[12]) for sign extension.
                imm := (others => instruction_i(31));
                -- Place fragmented immediate bits into their correct positions.
                imm(12)        := instruction_i(31);         -- imm[12]
                imm(11)        := instruction_i(7);          -- imm[11]
                imm(10 downto 5) := instruction_i(30 downto 25); -- imm[10:5]
                imm(4 downto 1) := instruction_i(11 downto 8);  -- imm[4:1]
                imm(0)         := '0';                       -- imm[0] is always 0 for branches
                -- Assign the constructed immediate to the output.
                immediate_o <= imm;

            -- U-type immediate (LUI, AUIPC)
            -- Opcode values: 0x37 (LUI), 0x17 (AUIPC)
            -- Format: imm[31:12] is instruction[31:12]
            -- This immediate is already effectively shifted left by 12 bits.
            when "0110111" | "0010111" =>
                -- Concatenate the upper 20 bits of the instruction with 12 zeros.
                -- No explicit sign extension needed, as the value is simply the upper bits.
                imm := instruction_i(31 downto 12) & (11 downto 0 => '0');
                -- Assign the constructed immediate to the output.
                immediate_o <= imm;

            -- J-type immediate (JAL)
            -- Opcode value: 0x6F (JAL)
            -- Format: imm[20|10:1|11|19:12]
            -- Bits: instruction[31] (imm[20]), instruction[19:12] (imm[19:12]),
            --       instruction[20] (imm[11]), instruction[30:21] (imm[10:1])
            -- Reconstructed: imm[20] << 20 | imm[19:12] << 12 | imm[11] << 11 | imm[10:1] << 1 (imm[0] is always '0')
            when "1101111" =>
                -- Sign-extend the 21-bit immediate: use bit 31 of the instruction
                -- (which is imm[20]) for sign extension.
                imm := (others => instruction_i(31));
                -- Place fragmented immediate bits into their correct positions.
                imm(20)        := instruction_i(31);         -- imm[20]
                imm(19 downto 12) := instruction_i(19 downto 12); -- imm[19:12]
                imm(11)        := instruction_i(20);         -- imm[11]
                imm(10 downto 1) := instruction_i(30 downto 21); -- imm[10:1]
                imm(0)         := '0';                       -- imm[0] is always 0 for jumps
                -- Assign the constructed immediate to the output.
                immediate_o <= imm;

            -- VECTOR_I_OP*
            when "1010100" | "1010101" | "1010110" =>
                imm := (others => instruction_i(31));
                imm(11 downto 0) := instruction_i(31 downto 20);
                immediate_o <= imm;

            -- VECTOR_U_OP*
            when "1011000" | "1011001" | "1011010" =>
                imm := instruction_i(31 downto 12) & (11 downto 0 => '0');
                immediate_o <= imm;

            -- VECTOR_R_OP*
            when "1010000" | "1010001" | "1010010" =>
                immediate_o <= (others => '0');

            -- Default case
            when others =>
                immediate_o <= (others => '0');
        end case;
    end process;

end architecture behavioral;
*/

/* Code of ID_EX_Pipeline:
library IEEE;
use IEEE.STD_LOGIC_1164.ALL;
use IEEE.NUMERIC_STD.ALL;

entity ID_EX_Pipeline is
    Port (
        clk           : in  std_logic;
        reset         : in  std_logic;

        -- Control signals
        ALUOp_in      : in  std_logic_vector(1 downto 0);
        ALUSrc_in     : in  std_logic;
        memRead_in   : in  std_logic;
        memWrite_in  : in  std_logic;
        memToReg_in  : in  std_logic_vector(1 downto 0);
        regWrite_in  : in  std_logic;
        -- Data signals
        Rs1_data_in  : in  std_logic_vector(31 downto 0);
        Rs2_data_in  : in  std_logic_vector(31 downto 0);
        Imm_in : in  std_logic_vector(31 downto 0);
        Rs1_in         : in  std_logic_vector(4 downto 0);
        Rs2_in         : in  std_logic_vector(4 downto 0);
        Rd_in         : in  std_logic_vector(4 downto 0);
        funct_3_in      : in  std_logic_vector(2 downto 0);
        funct_7_in      : in  std_logic_vector(6 downto 0); 
        
        bubble        : in std_logic; -- Input de bubble síncrono
        pc_in        : in std_logic_vector(31 downto 0);
        alu_pc_in    : in std_logic;
        pc4_in	     : in std_logic_vector(31 downto 0);
        immSrc_in    : in std_logic;
	size_in     : in  std_logic_vector(1 downto 0); -- Size for vector operations

        -- Control outputs
        ALUOp_out     : out std_logic_vector(1 downto 0);
        ALUSrc_out    : out std_logic;
        memRead_out   : out std_logic;
        memWrite_out  : out std_logic;
        memToReg_out  : out std_logic_vector(1 downto 0);
        regWrite_out  : out std_logic;
        -- Data outputs
        Rs1_data_out       : out std_logic_vector(31 downto 0);
        Rs2_data_out       : out std_logic_vector(31 downto 0);
        Imm_out       : out std_logic_vector(31 downto 0);
        Rs1_out       : out std_logic_vector(4 downto 0);
        Rs2_out       : out std_logic_vector(4 downto 0);
        Rd_out        : out std_logic_vector(4 downto 0);
        funct_3_out     : out  std_logic_vector(2 downto 0);
        funct_7_5     : out  std_logic;
        pc_out	      : out std_logic_vector(31 downto 0);
        alu_pc_out    : out std_logic;
        pc4_out       : out std_logic_vector(31 downto 0);
        immSrc_out    : out std_logic;
        size_out     : out std_logic_vector(1 downto 0) -- Size for vector operations
    );
end ID_EX_Pipeline;

architecture Behavioral of ID_EX_Pipeline is
begin
    process(clk, reset)
    begin
        if reset = '1' then
            -- On reset, clear all outputs
            ALUOp_out      <= (others => '0');
            ALUSrc_out     <= '0';
            memRead_out    <= '0';
            memWrite_out   <= '0';
            memToReg_out   <= "00";
            regWrite_out   <= '0';
            Rs1_data_out       <= (others => '0');
            Rs2_data_out       <= (others => '0');
            Imm_out       <= (others => '0');
            Rs1_out         <= (others => '0');
            Rs2_out         <= (others => '0');
            Rd_out         <= (others => '0');
            funct_3_out <= (others => '0');
            funct_7_5 <= '0';
            pc_out <= (others => '0');
            alu_pc_out <= '0';
            pc4_out <= (others => '0');
            immSrc_out <= '0';
            size_out <= (others => '0');
        elsif rising_edge(clk) then
            if bubble = '1' then
                ALUOp_out      <= (others => '0');
                ALUSrc_out     <= '0';
                memRead_out    <= '0';
                memWrite_out   <= '0';
                memToReg_out   <= "00";
                regWrite_out   <= '0';
                Rs1_data_out       <= (others => '0');
                Rs2_data_out       <= (others => '0');
                Imm_out       <= (others => '0');
                Rs1_out         <= (others => '0');
                Rs2_out         <= (others => '0');
                Rd_out         <= (others => '0');
                funct_3_out <= (others => '0');
                        funct_7_5 <= '0';
                pc_out <= (others => '0');
                alu_pc_out <= '0';
                pc4_out <= (others => '0');
                immSrc_out <= '0';
                size_out <= (others => '0');
            else
                -- On clock edge, latch inputs to outputs
                ALUOp_out      <= ALUOp_in;
                ALUSrc_out     <= ALUSrc_in;
                memRead_out    <= memRead_in;
                memWrite_out   <= memWrite_in;
                memToReg_out   <= memToReg_in;
                regWrite_out   <= regWrite_in;
                Rs1_data_out       <= Rs1_data_in;
                Rs2_data_out       <= Rs2_data_in;
                Imm_out       <= Imm_in;
                Rs1_out         <= Rs1_in;
                Rs2_out         <= Rs2_in;
                Rd_out         <= Rd_in;
                funct_3_out <= funct_3_in;
                funct_7_5 <= funct_7_in(5);
                pc_out <= pc_in;
                alu_pc_out <= alu_pc_in;
                pc4_out <= pc4_in;
                immSrc_out <= immSrc_in;
                size_out <= size_in;
            end if;
        end if;
    end process;
end Behavioral;
*/

/* Code of ALUControl:
library ieee;
use ieee.std_logic_1164.all;
use ieee.numeric_std.all;

entity ALUControl is
    port (
        ALUOp  : in  std_logic_vector(1 downto 0);
        funct3 : in  std_logic_vector(2 downto 0);
        funct7_5: in std_logic;  -- bit 30 da instrução (funct7[5])
	size : in std_logic_vector(1 downto 0); -- controle externo para operações vetoriais
        ALUCtrl : out std_logic_vector(4 downto 0)
    );
end entity;

architecture Behavioral of ALUControl is
begin
    process(ALUOp, funct3, funct7_5, size)
    begin
        case ALUOp is
            when "00" =>  -- Loads, Stores, AUIPC (ADD)
		case size is
			when "00" => 
				ALUCtrl <= "01000";  -- 04
			when "01" =>
				ALUCtrl <= "01001";  -- 08
			when "10" =>
				ALUCtrl <= "01010";  -- 16
			when "11" =>
				ALUCtrl <= "00010";  -- 32
			when others =>
               			ALUCtrl <= "11111";	
		end case;

            when "01" =>  -- Branches (SUB)
		case size is
			when "00" => 
				ALUCtrl <= "01100";  -- 04
			when "01" =>
				ALUCtrl <= "01101";  -- 08
			when "10" =>
				ALUCtrl <= "01110";  -- 16
			when "11" =>
				ALUCtrl <= "00110";  -- 32
			when others =>
               			ALUCtrl <= "11111";	
		end case;

            when "10" =>  -- R-Type instructions
                case funct3 is
                    when "000" =>  -- ADD or SUB
                        if funct7_5 = '0' then
				case size is
					when "00" => 
						ALUCtrl <= "01000";  -- 04
					when "01" =>
						ALUCtrl <= "01001";  -- 08
					when "10" =>
						ALUCtrl <= "01010";  -- 16
					when "11" =>
						ALUCtrl <= "00010";  -- 32
					when others =>
               					ALUCtrl <= "11111";	
				end case;

                        else
                            case size is
				when "00" => 
					ALUCtrl <= "01100";  -- 04
				when "01" =>
					ALUCtrl <= "01101";  -- 08
				when "10" =>
					ALUCtrl <= "01110";  -- 16
				when "11" =>
					ALUCtrl <= "00110";  -- 32
				when others =>
               				ALUCtrl <= "11111";	
			end case;
                        end if;
                    when "111" => ALUCtrl <= "00000"; -- AND
                    when "110" => ALUCtrl <= "00001"; -- OR
                    when "100" => ALUCtrl <= "00011"; -- XOR
                    when "001" => -- SLL
			case size is
				when "00" => 
					ALUCtrl <= "10000";  -- 04
				when "01" =>
					ALUCtrl <= "10001";  -- 08
				when "10" =>
					ALUCtrl <= "10010";  -- 16
				when "11" =>
					ALUCtrl <= "00100";  -- 32
				when others =>
               				ALUCtrl <= "11111";	
			end case;

                    when "101" => -- SRL
			case size is
				when "00" => 
					ALUCtrl <= "11000";  -- 04
				when "01" =>
					ALUCtrl <= "11001";  -- 08
				when "10" =>
					ALUCtrl <= "11010";  -- 16
				when "11" =>
					ALUCtrl <= "00101";  -- 32
				when others =>
               				ALUCtrl <= "11111";	
			end case;

                    when others =>
                        ALUCtrl <= "11111"; -- Default / não definido
                end case;

            when "11" =>  -- I-Type aritméticas e shifts imediatas
                case funct3 is
                    when "000" => 
			case size is
				when "00" => 
					ALUCtrl <= "01000";  -- 04
				when "01" =>
					ALUCtrl <= "01001";  -- 08
				when "10" =>
					ALUCtrl <= "01010";  -- 16
				when "11" =>
					ALUCtrl <= "00010";  -- 32
				when others =>
               				ALUCtrl <= "11111";	
			end case;

                    when "111" => ALUCtrl <= "00000"; -- ANDI
                    when "110" => ALUCtrl <= "00001"; -- ORI
                    when "100" => ALUCtrl <= "00011"; -- XORI
                    when "001" => -- SLLI
			case size is
				when "00" => 
					ALUCtrl <= "10000";  -- 04
				when "01" =>
					ALUCtrl <= "10001";  -- 08
				when "10" =>
					ALUCtrl <= "10010";  -- 16
				when "11" =>
					ALUCtrl <= "00100";  -- 32
				when others =>
               				 ALUCtrl <= "11111";	
			end case;

                    when "101" => -- SRLI
			case size is
				when "00" => 
					ALUCtrl <= "11000";  -- 04
				when "01" =>
					ALUCtrl <= "11001";  -- 08
				when "10" =>
					ALUCtrl <= "11010";  -- 16
				when "11" =>
					ALUCtrl <= "00101";  -- 32
				when others =>
               				 ALUCtrl <= "11111";		
			end case;

                    when others =>
                        ALUCtrl <= "11111"; -- Default / não definido
                end case;

            when others =>
                ALUCtrl <= "11111"; -- Default / não definido
        end case;
    end process;
end architecture;
*/

/* Code of forwarding_unit:
library ieee;
use ieee.std_logic_1164.all;

-- The forwarding unit entity declaration
entity forwarding_unit is
    port (
        -- Inputs from pipeline registers
        -- Source registers for the instruction currently in the EX stage (for ALU operations)
        ID_EX_rs1        : in std_logic_vector(4 downto 0);
        ID_EX_rs2        : in std_logic_vector(4 downto 0);

        -- Source registers for the instruction currently in the ID stage (for Branch Comparison)
        IF_ID_rs1        : in std_logic_vector(4 downto 0);
        IF_ID_rs2        : in std_logic_vector(4 downto 0);

        -- Destination register for the instruction in the MEM stage
        EX_MEM_rd        : in std_logic_vector(4 downto 0);
        EX_MEM_RegWrite  : in std_logic; -- Control signal: Does the instruction in MEM write to a register?

        -- Destination register for the instruction in the WB stage
        MEM_WB_rd        : in std_logic_vector(4 downto 0);
        MEM_WB_RegWrite  : in std_logic; -- Control signal: Does the instruction in WB write to a register?

        -- Outputs: Control signals for the ALU input multiplexers (EX stage)
        -- 00: No forwarding (use ID/EX register value)
        -- 01: Forward from EX/MEM stage (ALU result)
        -- 10: Forward from MEM/WB stage (Memory data or older ALU result)
        ForwardA         : out std_logic_vector(1 downto 0);
        ForwardB         : out std_logic_vector(1 downto 0);

        -- New Outputs: Control signals for the Branch Comparison input multiplexers (ID stage)
        -- 00: No forwarding (use IF/ID register value from RegFile read)
        -- 01: Forward from EX/MEM stage (ALU result)
        -- 10: Forward from MEM/WB stage (Memory data or older ALU result)
        Forward_ID_A     : out std_logic_vector(1 downto 0);
        Forward_ID_B     : out std_logic_vector(1 downto 0)
    );
end entity forwarding_unit;

-- Architecture definition for the forwarding unit
architecture behavioral of forwarding_unit is
begin

    -- This process contains the combinational logic for the forwarding unit.
    -- It continuously checks for hazard conditions.
    process(ID_EX_rs1, ID_EX_rs2, IF_ID_rs1, IF_ID_rs2,
            EX_MEM_rd, EX_MEM_RegWrite, MEM_WB_rd, MEM_WB_RegWrite)
    begin
        -- Default to no forwarding for EX stage ALU
        ForwardA <= "00";
        ForwardB <= "00";

        -- Default to no forwarding for ID stage Branch Comparison
        Forward_ID_A <= "00";
        Forward_ID_B <= "00";

        -- --- FORWARDING LOGIC FOR OPERAND A (rs1) in EX stage (ALU) ---

        -- EX/MEM Hazard Check for EX stage rs1
        if (EX_MEM_RegWrite = '1') and
           (EX_MEM_rd /= "00000") and
           (EX_MEM_rd = ID_EX_rs1) then
            ForwardA <= "01"; -- Forward from EX/MEM 

        -- MEM/WB Hazard Check for EX stage rs1
        elsif (MEM_WB_RegWrite = '1') and
              (MEM_WB_rd /= "00000") and
              (MEM_WB_rd = ID_EX_rs1) then
            ForwardA <= "10"; -- Forward from MEM/WB 
        end if;


        -- --- FORWARDING LOGIC FOR OPERAND B (rs2) in EX stage (ALU) ---

        -- EX/MEM Hazard Check for EX stage rs2
        if (EX_MEM_RegWrite = '1') and
           (EX_MEM_rd /= "00000") and
           (EX_MEM_rd = ID_EX_rs2) then
            ForwardB <= "01"; -- Forward from EX/MEM

        -- MEM/WB Hazard Check for EX stage rs2
        elsif (MEM_WB_RegWrite = '1') and
              (MEM_WB_rd /= "00000") and
              (MEM_WB_rd = ID_EX_rs2) then
            ForwardB <= "10"; -- Forward from MEM/WB
        end if;


        -- OPERAND A (rs1) in ID stage (Branch Comparison) ---
        -- This logic is for instructions whose comparison is happening in the ID stage.
        -- These forwardings prevent stalls if the branch's operands are produced by
        -- instructions recently completed or currently in EX or MEM stages.

        -- Hazard with EX/MEM stage (most recent result) for ID stage rs1
        -- This means the result is available at the end of the EX stage.
        -- For a branch in ID, this requires bypassing the ALU result back to ID.
        if (EX_MEM_RegWrite = '1') and
           (EX_MEM_rd /= "00000") and
           (EX_MEM_rd = IF_ID_rs1) then
            Forward_ID_A <= "01"; -- Forward from EX/MEM pipeline register (ALU result)

        -- Hazard with MEM/WB stage for ID stage rs1
        -- This means the result is available at the end of the MEM stage.
        elsif (MEM_WB_RegWrite = '1') and
              (MEM_WB_rd /= "00000") and
              (MEM_WB_rd = IF_ID_rs1) then
            Forward_ID_A <= "10"; -- Forward from MEM/WB (Memory data or older ALU result)
        end if;


        -- OPERAND B (rs2) in ID stage (Branch Comparison) ---

        -- Hazard with EX/MEM stage for ID stage rs2
        if (EX_MEM_RegWrite = '1') and
           (EX_MEM_rd /= "00000") and
           (EX_MEM_rd = IF_ID_rs2) then
            Forward_ID_B <= "01"; -- Forward from EX/MEM pipeline register (ALU result)

        -- Hazard with MEM/WB stage for ID stage rs2
        elsif (MEM_WB_RegWrite = '1') and
              (MEM_WB_rd /= "00000") and
              (MEM_WB_rd = IF_ID_rs2) then
            Forward_ID_B <= "10"; -- Forward from MEM/WB (Memory data or older ALU result)
        end if;

    end process;

end architecture behavioral;
*/

/* Code of EX_MEM_Pipeline:
library IEEE;
use IEEE.STD_LOGIC_1164.ALL;
use IEEE.NUMERIC_STD.ALL;

entity EX_MEM_Pipeline is
    Port (
        clk          : in  std_logic;
        reset        : in  std_logic;

        -- Control signals
        MemRead_in   : in  std_logic;
        MemWrite_in  : in  std_logic;
        MemToReg_in  : in  std_logic_vector(1 downto 0);
        RegWrite_in  : in  std_logic;
        -- Data signals
        ALUResult_in : in  std_logic_vector(31 downto 0);
        WriteData_in : in  std_logic_vector(31 downto 0);
        Rd_in       : in  std_logic_vector(4 downto 0);
        bubble       : in std_logic; -- Entrada de bubble síncrona
	pc_in        : in std_logic_vector(31 downto 0);

        -- Outputs to MEM stage
        MemRead_out  : out std_logic;
        MemWrite_out : out std_logic;
        MemToReg_out : out std_logic_vector(1 downto 0);
        RegWrite_out : out std_logic;
        ALUResult_out: out std_logic_vector(31 downto 0);
        WriteData_out: out std_logic_vector(31 downto 0);
        Rd_out       : out std_logic_vector(4 downto 0);
	pc_out	     : out std_logic_vector(31 downto 0)
    );
end EX_MEM_Pipeline;

architecture Behavioral of EX_MEM_Pipeline is
begin
    process(clk, reset)
    begin
        if reset = '1' then
            MemRead_out   <= '0';
            MemWrite_out  <= '0';
            RegWrite_out  <= '0';
            MemToReg_out  <= "00";
            ALUResult_out <= (others => '0');
            WriteData_out <= (others => '0');
            Rd_out   <= (others => '0');
	    pc_out   <= (others => '0');
        elsif rising_edge(clk) then
            if bubble = '1' then

                MemRead_out   <= '0';
                MemWrite_out  <= '0';
                RegWrite_out  <= '0';
                MemToReg_out  <= "00";
                ALUResult_out <= (others => '0');
                WriteData_out <= (others => '0');
                Rd_out   <= (others => '0');
		pc_out   <= (others => '0');

            else
                MemRead_out   <= MemRead_in;
                MemWrite_out  <= MemWrite_in;
                RegWrite_out  <= RegWrite_in;
                MemToReg_out  <= MemToReg_in;
                ALUResult_out <= ALUResult_in;
                WriteData_out <= WriteData_in;
                Rd_out   <= Rd_in;
		pc_out   <= pc_in;
            end if;
        end if;
    end process;
end Behavioral;
*/

/* Code of addr_trunc32to24:
library IEEE;
use IEEE.STD_LOGIC_1164.ALL;

entity addr_trunc32to24 is
    Port (
        addr_32 : in  STD_LOGIC_VECTOR(31 downto 0);
        addr_24 : out STD_LOGIC_VECTOR(23 downto 0)
    );
end addr_trunc32to24;

architecture Behavioral of addr_trunc32to24 is
begin
    -- Pass lower 24 bits
    addr_24 <= addr_32(23 downto 0);
end Behavioral;
*/

/* Code of MEM_WB_Pipeline:
library IEEE;
use IEEE.STD_LOGIC_1164.ALL;
use IEEE.NUMERIC_STD.ALL;

entity MEM_WB_Pipeline is
    Port (
        clk           : in  std_logic;
        reset         : in  std_logic;
        -- Control signals
        MemToReg_in   : in  std_logic_vector(1 downto 0);
        RegWrite_in   : in  std_logic;
        -- Data signals
        ReadData_in   : in  std_logic_vector(31 downto 0);
        ALUResult_in  : in  std_logic_vector(31 downto 0);
        Rd_in         : in  std_logic_vector(4 downto 0);
	pc_in         : in std_logic_vector(31 downto 0);

        -- Outputs to WB stage
        MemToReg_out  : out std_logic_vector(1 downto 0);
        RegWrite_out  : out std_logic;
        ALUResult_out : out std_logic_vector(31 downto 0);
        ReadData_out  : out std_logic_vector(31 downto 0);
        Rd_out   : out std_logic_vector(4 downto 0);
	pc_out   : out std_logic_vector(31 downto 0)
    );
end MEM_WB_Pipeline;

architecture Behavioral of MEM_WB_Pipeline is
begin
    process(clk, reset)
    begin
        if reset = '1' then
            RegWrite_out  <= '0';
            MemToReg_out  <= "00";
            ReadData_out  <= (others => '0');
            ALUResult_out <= (others => '0');
            Rd_out   <= (others => '0');
	    pc_out   <= (others => '0');
        elsif rising_edge(clk) then
            RegWrite_out  <= RegWrite_in;
            MemToReg_out  <= MemToReg_in;
            ReadData_out  <= ReadData_in;
            ALUResult_out <= ALUResult_in;
            Rd_out   <= Rd_in;
	    pc_out   <= pc_in;
        end if;
    end process;
end Behavioral;
*/
