// Digital circuit Alu_com_somador_vetorial.dig as structural Verilog
module Alu_com_somador_vetorial (
  input  [31:0] a,
  input  [31:0] b,
  input  [4:0] c,
  output [31:0] result_out,
  output zero_out
);

  wire u_alu_combinational_zero_flag_out, u_vector_adder_zero_out, u_vector_shifter_zero_out;
  wire [31:0] u_alu_combinational_result_out, u_vector_adder_s_o, u_vector_shifter_s_o;

  alu_combinational #(.applicationType("GHDL")) u_alu_combinational (
    .a_in(a), .b_in(b), .c_in(c[3:0]), .result_out(u_alu_combinational_result_out),
    .zero_flag_out(u_alu_combinational_zero_flag_out));
  vector_adder #(.applicationType("GHDL")) u_vector_adder (
    .A_i(a), .B_i(b), .mode_i(c[2]), .vecSize_i(c[1:0]), .S_o(u_vector_adder_s_o),
    .zero_out(u_vector_adder_zero_out));
  vector_shifter #(.applicationType("GHDL")) u_vector_shifter (
    .A_i(a), .B_i(b), .mode_i(c[3]), .vecSize_i(c[1:0]), .S_o(u_vector_shifter_s_o),
    .zero_out(u_vector_shifter_zero_out));
  Multiplexer #(.Selector_Bits(2), .Bits(32)) multiplexer_1 (
    .sel(c[4:3]), .in_0(u_alu_combinational_result_out), .in_1(u_vector_adder_s_o),
    .in_2(u_vector_shifter_s_o), .in_3(u_vector_shifter_s_o), .out(result_out));
  Multiplexer #(.Selector_Bits(2)) multiplexer_2 (
    .sel(c[4:3]), .in_0(u_alu_combinational_zero_flag_out), .in_1(u_vector_adder_zero_out),
    .in_2(u_vector_shifter_zero_out), .in_3(u_vector_shifter_zero_out), .out(zero_out));
endmodule

/* Code of alu_combinational:
library IEEE;
use IEEE.STD_LOGIC_1164.ALL;
use IEEE.NUMERIC_STD.ALL;

entity alu_combinational is
    Port (
        a_in            : in  std_logic_vector(31 downto 0);
        b_in            : in  std_logic_vector(31 downto 0);
        c_in            : in  std_logic_vector(3 downto 0);
        result_out      : out std_logic_vector(31 downto 0);
        zero_flag_out   : out std_logic
    );
end alu_combinational;

architecture Behavioral of alu_combinational is

constant ALL_ZEROS_32 : std_logic_vector(31 downto 0) := (others => '0');

begin

    process(a_in, b_in, c_in)
        variable temp_result : std_logic_vector(31 downto 0);
    begin
        -- Initialize temp_result for safety (though not strictly necessary for full case coverage)
        temp_result := (others => '0');

        case c_in is
            when "0000" =>
                temp_result := a_in and b_in;
            when "0001" =>
                temp_result := a_in or b_in;
            when "0011" =>
                temp_result := a_in xor b_in;
            when "0010" =>
                temp_result := std_logic_vector(unsigned(a_in) + unsigned(b_in));
            when "0110" =>
                -- For subtraction, ensure both operands are treated as unsigned for consistent arithmetic.
                -- If signed subtraction is intended, use signed types for both a_in and b_in.
                temp_result := std_logic_vector(unsigned(a_in) - unsigned(b_in));
            when "0100" =>
                -- For shift operations, the shift amount should be an integer,
                -- and using 'unsigned' directly on the slice ensures proper conversion.
                temp_result := std_logic_vector(shift_left(unsigned(a_in), to_integer(unsigned(b_in(4 downto 0)))));
            when "0101" =>
                temp_result := std_logic_vector(shift_right(unsigned(a_in), to_integer(unsigned(b_in(4 downto 0)))));
            when others =>
                temp_result := (others => '0'); -- Default or undefined operation
        end case;

        -- Assign the calculated temporary result to the output signal
        result_out <= temp_result;

        -- Determine the zero flag based on the calculated result
        if temp_result = ALL_ZEROS_32 then
            zero_flag_out <= '1';
        else
            zero_flag_out <= '0';
        end if;

    end process;

end Behavioral;
*/

/* Code of vector_adder:
-- Ideia
-- Ter 8 somadores de 4 bits com carry lookahead. Assim, o carry se propaga de 4 em 4 em vez de se propagar de 1 em 1
-- Ao instanciar os somadores, propagar carry apenas no meio dos blocos (dependendo de vecSize_i). No início dos blocos, colocar carry '0' para adição. Para subtração, inverter todos os bits de B, e colocar carry '1' no início de cada bloco.

library IEEE;
use IEEE.STD_LOGIC_1164.ALL;

entity vector_adder is
    Port(
        A_i       : in  std_logic_vector(31 downto 0);
        B_i       : in  std_logic_vector(31 downto 0);
        mode_i    : in  std_logic; -- '0' para soma, '1' para subtração
        vecSize_i : in  std_logic_vector(1 downto 0); -- 00:4b, 01:8b, 10:16b, 11:32b
        S_o       : out std_logic_vector(31 downto 0);
	zero_out  : out std_logic
    );
end vector_adder;

architecture Behavioral of vector_adder is
    signal not_B: std_logic_vector(31 downto 0);
    signal carry: std_logic_vector(8 downto 0); -- O último carry é descartado

    component adder4 is
        Port(
            A: in std_logic_vector(3 downto 0);
            B: in std_logic_vector(3 downto 0);
            Cin: in std_logic;

            S: out std_logic_vector(3 downto 0);
            Cout: out std_logic
        );
    end component;

begin
    not_B <= not(B_i); -- Calculado uma vez só, para não ser necessário um conjunto de portas not por somador

    -- Instanciar os 8 somadores
    adder_generate: for i in 0 to 7 generate

        signal prop: std_logic;
        signal actual_carry: std_logic;
        signal B: std_logic_vector(3 downto 0);

    begin
        -- Propagar carry apenas no meio dos blocos
        prop <=
            '1' when
                ((vecSize_i = "01") and (i mod 2 /= 0)) or -- Blocos de 8, os adders se juntam de 2 em 2
                ((vecSize_i = "10") and (i mod 4 /= 0)) or -- Blocos de 16, os adders se juntam de 4 em 4
                ((vecSize_i = "11") and (i /= 0)) -- Bloco de 32, todos os 8 adders se juntam

                -- com vecSize_i = "00", não há propagação
            else '0';

        -- No meio dos blocos, propagamos carry. No início dos blocos, colocamos carry '0' para soma e carry '1' para subtração (complemento de 2)
        actual_carry <=
            carry(i) when prop = '1'
            else mode_i;

        B <=
            B_i(4*i+3 downto 4*i) when mode_i = '0'
            else not_B(4*i+3 downto 4*i);

        adder: adder4
        port map(
            A => A_i(4*i+3 downto 4*i),

            B => B,
            
            Cin => actual_carry,
            
            S => S_o(4*i+3 downto 4*i),

            Cout => carry(i+1)
        );
    end generate;

	process(S_o)
    	begin
        	if S_o = X"00000000" then
    			zero_out <= '1';
		else
    			zero_out <= '0';
		end if;
        end process;

	
end Behavioral;

library IEEE;
use IEEE.STD_LOGIC_1164.ALL;

entity adder4 is
    Port(
        A: in std_logic_vector(3 downto 0);
        B: in std_logic_vector(3 downto 0);
        Cin: in std_logic;

        S: out std_logic_vector(3 downto 0);
        Cout: out std_logic
    );
end adder4;

architecture arch of adder4 is

    signal prop: std_logic_vector(3 downto 0);
    signal gen: std_logic_vector(3 downto 0);
    signal carry: std_logic_vector(3 downto 0);

begin

    signals_generate: for i in 0 to 3 generate
        prop(i) <= A(i) xor B(i);
        gen(i) <= A(i) and B(i);
    end generate;

    -- Carry lookahead
    carry(0) <= Cin;
    carry(1) <= gen(0) or (prop(0) and Cin);

    carry(2) <= gen(1) or (prop(1) and gen(0)) or (prop(1) and prop(0) and Cin);

    carry(3) <= gen(2) or (prop(2) and gen(1)) or (prop(2) and prop(1) and gen(0)) or (prop(2) and prop(1) and prop(0) and Cin);

    Cout <= gen(3) or (prop(3) and gen(2)) or (prop(3) and prop(2) and gen(1)) or (prop(3) and prop(2) and prop(1) and gen(0)) or (prop(3) and prop(2) and prop(1) and prop(0) and Cin);

    sum_generate: for i in 0 to 3 generate
        S(i) <= prop(i) xor carry(i);
    end generate;

end arch;
*/

/* Code of vector_shifter:
library IEEE;
use IEEE.STD_LOGIC_1164.ALL;
use IEEE.NUMERIC_STD.ALL;

entity vector_shifter is
    Port(
        A_i       : in  std_logic_vector(31 downto 0);
        B_i       : in  std_logic_vector(31 downto 0);  -- rs2 ou imediato
        mode_i    : in  std_logic;                      -- '0' = shift left, '1' = shift right
        vecSize_i : in  std_logic_vector(1 downto 0);   -- 00:4b, 01:8b, 10:16b, 11:32b
        S_o       : out std_logic_vector(31 downto 0);
	zero_out  : out std_logic
    );
end vector_shifter;

architecture Behavioral of vector_shifter is

    signal result : std_logic_vector(31 downto 0);
    signal shamt  : std_logic_vector(4 downto 0);
    signal shamt_int : integer;
    constant ALL_ZEROS_32 : std_logic_vector(31 downto 0) := (others => '0');

begin

    -- Pega os 5 LSBs do B_i como shift amount
    shamt <= B_i(4 downto 0);
    shamt_int <= to_integer(unsigned(shamt));

    -- Processo único com geradores internos para diferentes tamanhos de vetores
    process(A_i, shamt_int, mode_i, vecSize_i)
        variable temp_result : std_logic_vector(31 downto 0);
	variable segment4 : std_logic_vector(3 downto 0);
    	variable segment8 : std_logic_vector(7 downto 0);
    	variable segment16 : std_logic_vector(15 downto 0);
    begin
        temp_result := (others => '0');

        case vecSize_i is

            when "00" =>  -- 4-bit vetores (8 grupos)
                gen4: for i in 0 to 7 loop
		if shamt_int >= 4 then
            		segment4 := (others => '0');
		else
                    if mode_i = '0' then
                        segment4 := std_logic_vector(shift_left(unsigned(A_i(4*i+3 downto 4*i)), shamt_int mod 4));
                    else
                        segment4 := std_logic_vector(shift_right(unsigned(A_i(4*i+3 downto 4*i)), shamt_int mod 4));
                    end if;
		end if;
                    temp_result(4*i+3 downto 4*i) := segment4;
                end loop;

            when "01" =>  -- 8-bit vetores (4 grupos)
                gen8: for i in 0 to 3 loop
		if shamt_int >= 8 then
            		segment8 := (others => '0');
		else
                    if mode_i = '0' then
                        segment8 := std_logic_vector(shift_left(unsigned(A_i(8*i+7 downto 8*i)), shamt_int mod 8));
                    else
                        segment8 := std_logic_vector(shift_right(unsigned(A_i(8*i+7 downto 8*i)), shamt_int mod 8));
                    end if;
                    temp_result(8*i+7 downto 8*i) := segment8;
		end if;
                end loop;

            when "10" =>  -- 16-bit vetores (2 grupos)
                gen16: for i in 0 to 1 loop
		if shamt_int >= 16 then
            		segment16 := (others => '0');
		else
                    if mode_i = '0' then
                        segment16 := std_logic_vector(shift_left(unsigned(A_i(16*i+15 downto 16*i)), shamt_int mod 16));
                    else
                        segment16 := std_logic_vector(shift_right(unsigned(A_i(16*i+15 downto 16*i)), shamt_int mod 16));
                    end if;
                    temp_result(16*i+15 downto 16*i) := segment16;
		end if;
                end loop;

            when others =>  -- 32-bit vetor (1 grupo)
                if mode_i = '0' then
                    temp_result := std_logic_vector(shift_left(unsigned(A_i), shamt_int mod 32));
                else
                    temp_result := std_logic_vector(shift_right(unsigned(A_i), shamt_int mod 32));
                end if;

        end case;

        S_o <= temp_result;
	if temp_result = ALL_ZEROS_32 then
            zero_out <= '1';
        else
            zero_out <= '0';
        end if;

    end process;

end Behavioral;
*/
