// Digital circuit novoblocoIF2.dig as structural Verilog
module novoblocoIF2 (
  input  jump,
  input  [31:0] jump_pc,
  input  [31:0] pc_in,
  output [23:0] inst_addr,
  output [31:0] pc_out,
  output [31:0] PC_plus_4
);

  Multiplexer #(.Bits(32)) multiplexer_1 (.sel(jump), .in_0(PC_plus_4), .in_1(jump_pc), .out(pc_out));
  adder adder_1 (.A(32'h4), .B(pc_in), .S(PC_plus_4));
  pc_to_addr #(.applicationType("GHDL")) u_pc_to_addr (.pc_i(pc_in), .addr_o(inst_addr));

  // Notes on the sheet:
  //   jump_pc: Valor do PC para o qual devemos dar jump
  //   pc_out: Deve ir para a entrada de PC, para ser escrito na próxima subida de clock.
  //   pc_in: É o valor atual de PC, que vai ser usado para calcular PC+4 e endereçar a memória de instrução.
endmodule

/* Code of pc_to_addr:
-- Recebe pc(31 downto 0) e retorna pc(25 downto 2), para ser usado como endereco da memória de instrução.

-- Isso ocorre porque a memória de instrução do Digital só recebe 24 bits de endereço. Para facilitar ao máximo a gente editar a memória de instrução e fazer testes, vou configurar a memória de instrução com 24 bits de endereço e 32 bits por palavra.
-- Como os últimos 2 bits de PC são ignorados, quando somamos PC+4, estamos indo para a próxima palavra de 32 bits da memória de instrução.

library IEEE;
use IEEE.STD_LOGIC_1164.ALL;

entity pc_to_addr is
	Port (
    	pc_i : in std_logic_vector(31 downto 0);
    	
        addr_o: out std_logic_vector(23 downto 0)
    	);
end pc_to_addr;

architecture Behavioral of pc_to_addr is

begin

process(pc_i)
begin
    addr_o <= pc_i(25 downto 2);
end process;

end Behavioral;
*/
