// Digital circuit somador4_test.dig as structural Verilog
module somador4_test (
  input  [3:0] in_1,
  input  [3:0] in_2,
  input  in_3,
  output [3:0] out_4,
  output out_5
);

  somador4 #(.applicationType("GHDL")) u_somador4 (.A(in_1), .B(in_2), .Cin(in_3), .S(out_4), .Cout(out_5));
endmodule

/* Code of somador4:
-- Ideia
-- Ter 8 somadores de 4 bits com carry lookahead. Assim, o carry se propaga de 4 em 4 em vez de se propagar de 1 em 1
-- Ter um módulo carry-enable, que recebe mode_i, vec_size_i, o índice do somador (0 a 7) e Cin e determina qual carry realmente vai para o somador (pode ter que frear propagação devido à separação em blocos, ou então forçar o carry em 1 para subtração)

library IEEE;
use IEEE.STD_LOGIC_1164.ALL;

entity somador4 is
    Port(
        A: in std_logic_vector(3 downto 0);
        B: in std_logic_vector(3 downto 0);
        Cin: in std_logic;

        S: out std_logic_vector(3 downto 0);
        Cout: out std_logic
    );
end somador4;

architecture Behavioral of somador4 is

    signal prop: std_logic_vector(3 downto 0);
    signal gen: std_logic_vector(3 downto 0);
    signal carry: std_logic_vector(3 downto 0);

begin

    signals_generate: for i in 0 to 3 generate
        prop(i) <= A(i) xor B(i);
        gen(i) <= A(i) and B(i);
    end generate;

    -- Carry lookahead
    carry(0) <= Cin;
    carry(1) <= gen(0) or (prop(0) and Cin);

    carry(2) <= gen(1) or (prop(1) and gen(0)) or (prop(1) and prop(0) and Cin);

    carry(3) <= gen(2) or (prop(2) and gen(1)) or (prop(2) and prop(1) and gen(0)) or (prop(2) and prop(1) and prop(0) and Cin);

    Cout <= gen(3) or (prop(3) and gen(2)) or (prop(3) and prop(2) and gen(1)) or (prop(3) and prop(2) and prop(1) and gen(0)) or (prop(3) and prop(2) and prop(1) and prop(0) and Cin);

    sum_generate: for i in 0 to 3 generate
        S(i) <= prop(i) xor carry(i);
    end generate;

end Behavioral;
*/
