// Digital circuit estagioIF.dig as structural Verilog
module estagioIF (
  input  jump_i,
  input  [31:0] jump_pc,
  input  clk,
  input  reset,
  output [31:0] pc_o,
  output [31:0] inst_o
);

  wire [23:0] blocoif_1_p5;
  wire [31:0] blocoif_1_p6, inst_memory_d;

  // blocoIF blocoif_1: pin names not known; wires that end beside it: jump_i, jump_pc, clk, reset, blocoif_1_p5, blocoif_1_p6
  ROM #(.AddrBits(24), .Bits(32)) inst_memory (.A(blocoif_1_p5), .sel(1'b1), .D(inst_memory_d));
  IFID #(.applicationType("GHDL")) u_IFID (
    .pc_i(blocoif_1_p6), .inst_i(inst_memory_d), .clk(clk), .reset(reset), .pc_o(pc_o), .inst_o(inst_o));

  // Notes on the sheet:
  //   jump_pc: Valor de pc para o qual devemos dar jump
  //   pc_o: Saída PC do registrador IF/ID
  //   inst_o: Saída de instrução do registrador IF/ID
endmodule

/* Code of IFID:
-- Registrador que guarda os dados necessários entre IF e ID. Esses dados são o valor de PC e a instrução da vez
library IEEE;
use IEEE.STD_LOGIC_1164.ALL;

entity IFID is
	Port (
    	pc_i : in std_logic_vector(31 downto 0);
        inst_i: in std_logic_vector(31 downto 0);

    	clk: in std_logic;
        reset: in std_logic;

        pc_o: out std_logic_vector(31 downto 0);
        inst_o: out std_logic_vector(31 downto 0)
    	);
end IFID;

architecture Behavioral of IFID is

begin

process(clk, reset)
begin
	if reset = '1' then
        pc_o <= X"00000000";
        inst_o <= X"00000000";
	else
		if clk'event and clk = '1' then
			pc_o <= pc_i;
            inst_o <= inst_i;
		end if;
	end if;
end process;

end Behavioral;
*/
